// Logisim project BCD Logisim.circ as structural Verilog: 2 circuits, main circuit main
module main (
  input  A13,
  input  A12,
  input  A11,
  input  A10,
  input  A9,
  input  A8,
  input  A7,
  input  A6,
  input  A5,
  input  A4,
  input  A3,
  input  A2,
  input  A1,
  input  A0,
  output [3:0] out_15,
  output [3:0] out_16,
  output [3:0] out_17,
  output [3:0] out_18,
  output [3:0] out_19
);

  wire bcd_1_s1, bcd_1_s2, bcd_1_s3, bcd_2_s1, bcd_2_s2, bcd_2_s3, bcd_4_s0, bcd_4_s1, bcd_4_s2, bcd_4_s3,
       bcd_5_s0, bcd_5_s1, bcd_5_s2, bcd_5_s3, bcd_6_s0, bcd_6_s1, bcd_6_s2, bcd_6_s3, bcd_7_s0, bcd_7_s1,
       bcd_7_s2, bcd_7_s3, bcd_8_s0, bcd_8_s1, bcd_8_s2, bcd_8_s3, bcd_9_s0, bcd_9_s1, bcd_9_s2, bcd_9_s3,
       bcd_10_s0, bcd_10_s1, bcd_10_s2, bcd_10_s3, bcd_11_s0, bcd_11_s1, bcd_11_s2, bcd_11_s3, bcd_12_s0,
       bcd_12_s1, bcd_12_s2, bcd_12_s3, bcd_13_s0, bcd_13_s1, bcd_13_s2, bcd_13_s3, bcd_14_s0, bcd_14_s1,
       bcd_14_s2, bcd_14_s3, bcd_16_s0, bcd_16_s1, bcd_16_s2, bcd_16_s3, bcd_17_s0, bcd_17_s1, bcd_17_s2,
       bcd_17_s3, bcd_18_s0, bcd_18_s1, bcd_18_s2, bcd_18_s3, bcd_19_s0, bcd_19_s1, bcd_19_s2, bcd_19_s3,
       bcd_20_s0, bcd_20_s1, bcd_20_s2, bcd_20_s3, bcd_21_s0, bcd_21_s1, bcd_21_s2, bcd_21_s3, bcd_22_s0,
       bcd_22_s1, bcd_22_s2, bcd_22_s3, bcd_23_s0, bcd_23_s1, bcd_23_s2, bcd_23_s3, bcd_24_s0, bcd_24_s1,
       bcd_24_s2, bcd_24_s3, bcd_25_s0, bcd_25_s1, bcd_25_s2, bcd_25_s3, bcd_27_s0, bcd_27_s1, bcd_27_s2,
       bcd_27_s3, bcd_28_s0, bcd_28_s1, bcd_28_s2, bcd_28_s3, bcd_29_s0, bcd_29_s1, bcd_29_s2, bcd_29_s3;

  BCD bcd_1 (
    .A3(bcd_6_s0), .A2(bcd_5_s0), .A1(bcd_4_s0), .A0(1'b0), .S3(bcd_1_s3), .S2(bcd_1_s2), .S1(bcd_1_s1),
    .S0(out_16[1]));
  BCD bcd_2 (
    .A3(bcd_9_s0), .A2(bcd_1_s3), .A1(bcd_1_s2), .A0(bcd_1_s1), .S3(bcd_2_s3), .S2(bcd_2_s2), .S1(bcd_2_s1),
    .S0(out_16[0]));
  BCD bcd_3 (
    .A3(bcd_10_s0), .A2(bcd_2_s3), .A1(bcd_2_s2), .A0(bcd_2_s1), .S3(out_19[0]), .S2(out_19[1]),
    .S1(out_19[2]), .S0(out_19[3]));
  BCD bcd_4 (
    .A3(bcd_13_s0), .A2(bcd_8_s0), .A1(bcd_7_s0), .A0(1'b0), .S3(bcd_4_s3), .S2(bcd_4_s2), .S1(bcd_4_s1),
    .S0(bcd_4_s0));
  BCD bcd_5 (
    .A3(bcd_14_s0), .A2(bcd_4_s3), .A1(bcd_4_s2), .A0(bcd_4_s1), .S3(bcd_5_s3), .S2(bcd_5_s2), .S1(bcd_5_s1),
    .S0(bcd_5_s0));
  BCD bcd_6 (
    .A3(bcd_19_s0), .A2(bcd_5_s3), .A1(bcd_5_s2), .A0(bcd_5_s1), .S3(bcd_6_s3), .S2(bcd_6_s2), .S1(bcd_6_s1),
    .S0(bcd_6_s0));
  BCD bcd_7 (
    .A3(bcd_16_s0), .A2(bcd_12_s0), .A1(bcd_11_s0), .A0(1'b0), .S3(bcd_7_s3), .S2(bcd_7_s2), .S1(bcd_7_s1),
    .S0(bcd_7_s0));
  BCD bcd_8 (
    .A3(bcd_17_s0), .A2(bcd_7_s3), .A1(bcd_7_s2), .A0(bcd_7_s1), .S3(bcd_8_s3), .S2(bcd_8_s2), .S1(bcd_8_s1),
    .S0(bcd_8_s0));
  BCD bcd_9 (
    .A3(bcd_20_s0), .A2(bcd_6_s3), .A1(bcd_6_s2), .A0(bcd_6_s1), .S3(bcd_9_s3), .S2(bcd_9_s2), .S1(bcd_9_s1),
    .S0(bcd_9_s0));
  BCD bcd_10 (
    .A3(bcd_21_s0), .A2(bcd_9_s3), .A1(bcd_9_s2), .A0(bcd_9_s1), .S3(bcd_10_s3), .S2(bcd_10_s2),
    .S1(bcd_10_s1), .S0(bcd_10_s0));
  BCD bcd_11 (.A3(A11), .A2(A12), .A1(A13), .A0(1'b0), .S3(bcd_11_s3), .S2(bcd_11_s2), .S1(bcd_11_s1), .S0(bcd_11_s0));
  BCD bcd_12 (
    .A3(A10), .A2(bcd_11_s3), .A1(bcd_11_s2), .A0(bcd_11_s1), .S3(bcd_12_s3), .S2(bcd_12_s2), .S1(bcd_12_s1),
    .S0(bcd_12_s0));
  BCD bcd_13 (
    .A3(bcd_18_s0), .A2(bcd_8_s3), .A1(bcd_8_s2), .A0(bcd_8_s1), .S3(bcd_13_s3), .S2(bcd_13_s2),
    .S1(bcd_13_s1), .S0(bcd_13_s0));
  BCD bcd_14 (
    .A3(bcd_23_s0), .A2(bcd_13_s3), .A1(bcd_13_s2), .A0(bcd_13_s1), .S3(bcd_14_s3), .S2(bcd_14_s2),
    .S1(bcd_14_s1), .S0(bcd_14_s0));
  BCD bcd_15 (
    .A3(bcd_22_s0), .A2(bcd_10_s3), .A1(bcd_10_s2), .A0(bcd_10_s1), .S3(out_18[0]), .S2(out_18[1]),
    .S1(out_18[2]), .S0(out_18[3]));
  BCD bcd_16 (
    .A3(A9), .A2(bcd_12_s3), .A1(bcd_12_s2), .A0(bcd_12_s1), .S3(bcd_16_s3), .S2(bcd_16_s2), .S1(bcd_16_s1),
    .S0(bcd_16_s0));
  BCD bcd_17 (
    .A3(A8), .A2(bcd_16_s3), .A1(bcd_16_s2), .A0(bcd_16_s1), .S3(bcd_17_s3), .S2(bcd_17_s2), .S1(bcd_17_s1),
    .S0(bcd_17_s0));
  BCD bcd_18 (
    .A3(A7), .A2(bcd_17_s3), .A1(bcd_17_s2), .A0(bcd_17_s1), .S3(bcd_18_s3), .S2(bcd_18_s2), .S1(bcd_18_s1),
    .S0(bcd_18_s0));
  BCD bcd_19 (
    .A3(bcd_24_s0), .A2(bcd_14_s3), .A1(bcd_14_s2), .A0(bcd_14_s1), .S3(bcd_19_s3), .S2(bcd_19_s2),
    .S1(bcd_19_s1), .S0(bcd_19_s0));
  BCD bcd_20 (
    .A3(bcd_25_s0), .A2(bcd_19_s3), .A1(bcd_19_s2), .A0(bcd_19_s1), .S3(bcd_20_s3), .S2(bcd_20_s2),
    .S1(bcd_20_s1), .S0(bcd_20_s0));
  BCD bcd_21 (
    .A3(bcd_27_s0), .A2(bcd_20_s3), .A1(bcd_20_s2), .A0(bcd_20_s1), .S3(bcd_21_s3), .S2(bcd_21_s2),
    .S1(bcd_21_s1), .S0(bcd_21_s0));
  BCD bcd_22 (
    .A3(bcd_28_s0), .A2(bcd_21_s3), .A1(bcd_21_s2), .A0(bcd_21_s1), .S3(bcd_22_s3), .S2(bcd_22_s2),
    .S1(bcd_22_s1), .S0(bcd_22_s0));
  BCD bcd_23 (
    .A3(A6), .A2(bcd_18_s3), .A1(bcd_18_s2), .A0(bcd_18_s1), .S3(bcd_23_s3), .S2(bcd_23_s2), .S1(bcd_23_s1),
    .S0(bcd_23_s0));
  BCD bcd_24 (
    .A3(A5), .A2(bcd_23_s3), .A1(bcd_23_s2), .A0(bcd_23_s1), .S3(bcd_24_s3), .S2(bcd_24_s2), .S1(bcd_24_s1),
    .S0(bcd_24_s0));
  BCD bcd_25 (
    .A3(A4), .A2(bcd_24_s3), .A1(bcd_24_s2), .A0(bcd_24_s1), .S3(bcd_25_s3), .S2(bcd_25_s2), .S1(bcd_25_s1),
    .S0(bcd_25_s0));
  BCD bcd_26 (
    .A3(bcd_29_s0), .A2(bcd_22_s3), .A1(bcd_22_s2), .A0(bcd_22_s1), .S3(out_17[0]), .S2(out_17[1]),
    .S1(out_17[2]), .S0(out_17[3]));
  BCD bcd_27 (
    .A3(A3), .A2(bcd_25_s3), .A1(bcd_25_s2), .A0(bcd_25_s1), .S3(bcd_27_s3), .S2(bcd_27_s2), .S1(bcd_27_s1),
    .S0(bcd_27_s0));
  BCD bcd_28 (
    .A3(A2), .A2(bcd_27_s3), .A1(bcd_27_s2), .A0(bcd_27_s1), .S3(bcd_28_s3), .S2(bcd_28_s2), .S1(bcd_28_s1),
    .S0(bcd_28_s0));
  BCD bcd_29 (
    .A3(A1), .A2(bcd_28_s3), .A1(bcd_28_s2), .A0(bcd_28_s1), .S3(bcd_29_s3), .S2(bcd_29_s2), .S1(bcd_29_s1),
    .S0(bcd_29_s0));
  BCD bcd_30 (
    .A3(A0), .A2(bcd_29_s3), .A1(bcd_29_s2), .A0(bcd_29_s1), .S3(out_15[0]), .S2(out_15[1]), .S1(out_15[2]),
    .S0(out_15[3]));

  assign out_16[3:2] = 2'b00;

  // Notes on the sheet:
  //   28
  //   28
  //   29
  //   10
  //   29
  //   30
  //   30
  //   4
  //   23
  //   24
  //   24
  //   25
  //   25
  //   26
  //   1
  //   6
  //   8
  //   17
  //   26
  //   27
  //   27
  //   2
  //   3
  //   18
  //   19
  //   5
  //   7
  //   9
  //   19
  //   20
  //   20
  //   21
  //   22
  //   11
  //   12
  //   13
  //   14
  //   15
  //   16
  //   10
  //   10
endmodule

module BCD (
  input  A3,
  input  A2,
  input  A1,
  input  A0,
  output S3,
  output S2,
  output S1,
  output S0
);

  wire and_1_out, and_2_out, and_3_out, and_4_out, and_5_out, and_6_out, and_7_out, and_8_out, and_9_out,
       and_10_out, and_11_out, and_12_out, and_13_out, and_14_out, and_15_out, not_1_out, not_2_out,
       not_3_out, not_4_out;

  not not_1 (not_1_out, A3);
  not not_2 (not_2_out, A2);
  not not_3 (not_3_out, A1);
  not not_4 (not_4_out, A0);
  and and_1 (and_1_out, not_1_out, not_2_out, A0);
  and and_2 (and_2_out, A2, A1, not_4_out);
  and and_3 (and_3_out, A3, not_2_out, not_4_out);
  and and_4 (and_4_out, A3, A2, A0);
  and and_5 (and_5_out, not_1_out, not_2_out, A1);
  and and_6 (and_6_out, A1, A0);
  and and_7 (and_7_out, A3, not_2_out, not_3_out, not_4_out);
  and and_8 (and_8_out, A3, A2, A0);
  and and_9 (and_9_out, A2, not_3_out, not_4_out);
  and and_10 (and_10_out, A3, not_2_out, A0);
  and and_11 (and_11_out, A3, A2, A1);
  and and_12 (and_12_out, not_1_out, A2, A0);
  and and_13 (and_13_out, not_1_out, A2, A1);
  and and_14 (and_14_out, A3, not_2_out, not_3_out);
  and and_15 (and_15_out, A3, not_3_out, not_4_out);
  or or_1 (S3, and_1_out, and_2_out, and_3_out, and_4_out);
  or or_2 (S2, and_5_out, and_6_out, and_7_out, and_8_out);
  or or_3 (S1, and_9_out, and_10_out, and_11_out);
  or or_4 (S0, and_12_out, and_13_out, and_14_out, and_15_out);
endmodule
