// Logisim project finalfinalfinalscroller.circ as structural Verilog: 1 circuit, main circuit main
module main (
  input  [3:0] in_1,
  input  [3:0] in_2,
  input  [3:0] in_3,
  input  [3:0] in_4,
  input  [3:0] in_5,
  output [3:0] out_6,
  output [3:0] out_7,
  output [3:0] out_8
);

  wire button_1_out, button_2_out, not_1_out, or_1_out;
  wire [1:0] counter_1_q;

  Button button_1 (.out(button_1_out));
  Button button_2 (.out(button_2_out));
  not not_1 (not_1_out, button_2_out);
  or or_1 (or_1_out, button_2_out, button_1_out);
  Multiplexer #(.select(2), .width(4), .enable("false")) multiplexer_1 (
    .in0(in_2), .in1(in_5), .in2(in_1), .in3(4'b0000), .out(out_6), .sel(counter_1_q));
  Multiplexer #(.select(2), .width(4), .enable("false")) multiplexer_2 (
    .in0(in_3), .in1(in_2), .in2(in_5), .in3(4'b0000), .out(out_7), .sel(counter_1_q));
  Multiplexer #(.select(2), .width(4), .enable("false")) multiplexer_3 (
    .in0(in_4), .in1(in_3), .in2(in_2), .in3(4'b0000), .out(out_8), .sel(counter_1_q));
  Counter #(.width(2), .max('h3)) counter_1 (
    .up(not_1_out), .clk(or_1_out), .Q(counter_1_q));  // open: clr, load, count, D, carry
endmodule
