// Logisim project logismMilestone2.circ as structural Verilog
module BinToBCD (
  input  A13,
  input  A12,
  input  A11,
  input  A10,
  input  A9,
  input  A8,
  input  A7,
  input  A6,
  input  A5,
  input  A4,
  input  A3,
  input  A2,
  input  A1,
  input  A0,
  output [3:0] U,
  output [3:0] T,
  output [3:0] H,
  output [3:0] TH,
  output [3:0] TT
);

  wire [0:0] bcd_8_x, bcd_13_x, bcd_15_x, bcd_16_x, bcd_17_x, bcd_18_x, bcd_19_x, bcd_21_x, bcd_22_x,
       bcd_23_x, bcd_24_x;
  wire [2:0] bcd_1_x, bcd_3_x, bcd_3_x_2, bcd_4_x, bcd_5_x, bcd_6_x, bcd_6_x_2, bcd_7_x, bcd_8_x_2, bcd_10_x,
       bcd_10_x_2, bcd_11_x, bcd_12_x, bcd_13_x_2, bcd_14_x, bcd_15_x_2, bcd_16_x_2, bcd_17_x_2, bcd_18_x_2,
       bcd_19_x_2, bcd_21_x_2, bcd_22_x_2, bcd_23_x_2;
  wire [3:0] bcd_25_x;
  wire [3:1] bcd_24_x_2;

  BCD bcd_1 (.a({1'b0, bcd_3_x}), .x({TT[1], bcd_1_x}));
  BCD bcd_2 (.a({bcd_1_x, bcd_8_x[0]}), .x({TT[0], TH[3:1]}));
  BCD bcd_3 (.a({1'b0, bcd_6_x}), .x({bcd_3_x[2], bcd_3_x_2}));
  BCD bcd_4 (.a({bcd_3_x_2, bcd_13_x[0]}), .x({bcd_3_x[1], bcd_4_x}));
  BCD bcd_5 (.a({bcd_4_x, bcd_17_x[0]}), .x({bcd_3_x[0], bcd_5_x}));
  BCD bcd_6 (.a({1'b0, bcd_10_x}), .x({bcd_6_x[2], bcd_6_x_2}));
  BCD bcd_7 (.a({bcd_6_x_2, bcd_15_x[0]}), .x({bcd_6_x[1], bcd_7_x}));
  BCD bcd_8 (.a({bcd_5_x, bcd_18_x[0]}), .x({bcd_8_x[0], bcd_8_x_2}));
  BCD bcd_9 (.a({bcd_8_x_2, bcd_19_x[0]}), .x({TH[0], H[3:1]}));
  BCD bcd_10 (.a({1'b0, A13, A12, A11}), .x({bcd_10_x[2], bcd_10_x_2}));
  BCD bcd_11 (.a({bcd_10_x_2, A10}), .x({bcd_10_x[1], bcd_11_x}));
  BCD bcd_12 (.a({bcd_7_x, bcd_16_x[0]}), .x({bcd_6_x[0], bcd_12_x}));
  BCD bcd_13 (.a({bcd_12_x, bcd_21_x[0]}), .x({bcd_13_x[0], bcd_13_x_2}));
  BCD bcd_14 (.a({bcd_11_x, A9}), .x({bcd_10_x[0], bcd_14_x}));
  BCD bcd_15 (.a({bcd_14_x, A8}), .x({bcd_15_x[0], bcd_15_x_2}));
  BCD bcd_16 (.a({bcd_15_x_2, A7}), .x({bcd_16_x[0], bcd_16_x_2}));
  BCD bcd_17 (.a({bcd_13_x_2, bcd_22_x[0]}), .x({bcd_17_x[0], bcd_17_x_2}));
  BCD bcd_18 (.a({bcd_17_x_2, bcd_23_x[0]}), .x({bcd_18_x[0], bcd_18_x_2}));
  BCD bcd_19 (.a({bcd_18_x_2, bcd_24_x[0]}), .x({bcd_19_x[0], bcd_19_x_2}));
  BCD bcd_20 (.a({bcd_19_x_2, bcd_25_x[3]}), .x({H[0], T[3:1]}));
  BCD bcd_21 (.a({bcd_16_x_2, A6}), .x({bcd_21_x[0], bcd_21_x_2}));
  BCD bcd_22 (.a({bcd_21_x_2, A5}), .x({bcd_22_x[0], bcd_22_x_2}));
  BCD bcd_23 (.a({bcd_22_x_2, A4}), .x({bcd_23_x[0], bcd_23_x_2}));
  BCD bcd_24 (.a({bcd_23_x_2, A3}), .x({bcd_24_x[0], bcd_24_x_2}));
  BCD bcd_25 (.a({bcd_24_x_2, A2}), .x(bcd_25_x));
  BCD bcd_26 (.a({bcd_25_x[2:0], A1}), .x({T[0], U[3:1]}));

  assign TT[3:2] = 2'b00;
  assign U[0] = A0;

  // Notes on the sheet:
  //   28
  //   28
  //   29
  //   10
  //   29
  //   4
  //   23
  //   24
  //   24
  //   25
  //   25
  //   26
  //   1
  //   6
  //   8
  //   17
  //   26
  //   2
  //   3
  //   18
  //   19
  //   5
  //   7
  //   9
  //   19
  //   20
  //   20
  //   21
  //   22
  //   11
  //   12
  //   13
  //   14
  //   15
  //   10
  //   10
endmodule

module mult8bit (
  input  [7:0] multiplicant,
  input  Button,
  input  CLK,
  input  [7:0] multiplier,
  output [13:0] out_5,
  output out_6,
  output out_7
);

  wire not_1_out, not_2_out, shift_register_2_p18, shift_register_2_p19, shift_register_2_p20,
       shift_register_2_p21, shift_register_2_p22, shift_register_2_p23, shift_register_2_p24;
  wire [6:0] multiplexer_1_out, multiplexer_2_out, negator_1_out, negator_2_out;
  wire [13:0] adder_1_out, multiplexer_3_out, shift_register_1_p13;

  Negator #(.width(7)) negator_1 (.in(multiplicant[6:0]), .out(negator_1_out));
  Multiplexer #(.width(7)) multiplexer_1 (
    .in0(multiplicant[6:0]), .in1(negator_1_out), .out(multiplexer_1_out), .sel(multiplicant[7]));
  Negator #(.width(7)) negator_2 (.in(multiplier[6:0]), .out(negator_2_out));
  not not_1 (not_1_out, Button);
  Multiplexer #(.width(7)) multiplexer_2 (
    .in0(multiplier[6:0]), .in1(negator_2_out), .out(multiplexer_2_out), .sel(multiplier[7]));
  // Shift_Register #(.length(14)) shift_register_1: pin names not known; wires that end beside it: Button, not_1_out, CLK, 1'b0, multiplexer_1_out[0], multiplexer_1_out[1], multiplexer_1_out[2], multiplexer_1_out[3], multiplexer_1_out[4], multiplexer_1_out[5], multiplexer_1_out[6], 1'b0, shift_register_1_p13[0], shift_register_1_p13[1], shift_register_1_p13[2], shift_register_1_p13[3], shift_register_1_p13[4], shift_register_1_p13[5], shift_register_1_p13[6], shift_register_1_p13[7]
  // Shift_Register #(.length(7)) shift_register_2: pin names not known; wires that end beside it: Button, not_1_out, CLK, 1'b0, multiplexer_2_out[6], multiplexer_2_out[5], multiplexer_2_out[4], multiplexer_2_out[3], multiplexer_2_out[2], multiplexer_2_out[1], multiplexer_2_out[0], 1'b0, 1'b0, 1'b0, 1'b0, 1'b0, 1'b0, shift_register_2_p18, shift_register_2_p19, shift_register_2_p20, shift_register_2_p21, shift_register_2_p22, shift_register_2_p23, shift_register_2_p24, shift_register_1_p13[8], shift_register_1_p13[9], shift_register_1_p13[10], shift_register_1_p13[11], shift_register_1_p13[12], shift_register_1_p13[13]
  nor nor_1 (out_7, shift_register_2_p18, shift_register_2_p19, shift_register_2_p20, shift_register_2_p21, shift_register_2_p22, shift_register_2_p23, shift_register_2_p24);
  Adder #(.width(14)) adder_1 (.a(out_5), .b(shift_register_1_p13), .out(adder_1_out), .cin(1'b0));  // open: cout
  Multiplexer #(.width(14)) multiplexer_3 (
    .in0(out_5), .in1(adder_1_out), .out(multiplexer_3_out), .sel(shift_register_2_p24));
  not not_2 (not_2_out, out_7);
  Register #(.width(14)) register_1 (.D(multiplexer_3_out), .en(not_2_out), .clk(CLK), .Q(out_5), .clr(Button));
  xor xor_1 (out_6, multiplier[7], multiplicant[7]);
endmodule

module BCD (
  input  [3:0] a,
  output [3:0] x
);

  wire and_1_out, and_2_out, and_3_out, and_4_out, and_5_out, and_6_out, and_7_out, and_8_out, and_9_out,
       and_10_out, and_11_out, not_1_out, not_2_out, not_3_out, not_4_out;

  not not_1 (not_1_out, a[3]);
  not not_2 (not_2_out, a[2]);
  not not_3 (not_3_out, a[1]);
  not not_4 (not_4_out, a[0]);
  and and_1 (and_1_out, a[2], a[0]);
  and and_2 (and_2_out, a[2], a[1]);
  or or_1 (x[3], and_1_out, and_2_out, and_3_out);
  and and_3 (and_3_out, a[3], not_2_out, not_3_out);
  and and_4 (and_4_out, a[2], not_3_out, not_4_out);
  or or_2 (x[2], and_4_out, and_5_out);
  and and_5 (and_5_out, a[3], a[0]);
  and and_6 (and_6_out, not_2_out, a[1]);
  and and_7 (and_7_out, a[1], a[0]);
  or or_3 (x[1], and_6_out, and_7_out, and_8_out);
  and and_8 (and_8_out, a[3], not_4_out);
  and and_9 (and_9_out, not_1_out, not_2_out, a[0]);
  and and_10 (and_10_out, a[2], a[1], not_4_out);
  or or_4 (x[0], and_9_out, and_10_out, and_11_out);
  and and_11 (and_11_out, a[3], not_4_out);
endmodule

module whole (
  input  [7:0] in_1,
  input  [7:0] in_2
);

  wire button_1_out, clock_1_out, d_ff_1_q, d_ff_2_q, decoder7segment_1_a, decoder7segment_1_b,
       decoder7segment_1_c, decoder7segment_1_d, decoder7segment_1_e, decoder7segment_1_f,
       decoder7segment_1_g, decoder7segment_2_a, decoder7segment_2_b, decoder7segment_2_c,
       decoder7segment_2_d, decoder7segment_2_e, decoder7segment_2_f, decoder7segment_2_g,
       decoder7segment_3_a, decoder7segment_3_b, decoder7segment_3_c, decoder7segment_3_d,
       decoder7segment_3_e, decoder7segment_3_f, decoder7segment_3_g, left_out, mult8bit_1_out_6,
       mult8bit_1_out_7, right_out;
  wire [3:0] bintobcd_1_h, bintobcd_1_t, bintobcd_1_th, bintobcd_1_tt, bintobcd_1_u, scroller_1_one,
       scroller_1_three, scroller_1_two;
  wire [13:0] mult8bit_1_out_5;

  Clock clock_1 (.out(clock_1_out));
  D_Flip_Flop d_ff_1 (.D(button_1_out), .clk(clock_1_out), .Q(d_ff_1_q));  // open: Qn, preset, reset
  Button button_1 (.out(button_1_out));
  D_Flip_Flop d_ff_2 (.D(d_ff_1_q), .clk(clock_1_out), .Q(d_ff_2_q));  // open: Qn, preset, reset
  mult8bit mult8bit_1 (
    .multiplicant(in_1), .Button(d_ff_2_q), .CLK(clock_1_out), .multiplier(in_2), .out_5(mult8bit_1_out_5),
    .out_6(mult8bit_1_out_6), .out_7(mult8bit_1_out_7));
  LED led_1 (.in(mult8bit_1_out_7));
  BinToBCD bintobcd_1 (
    .A13(mult8bit_1_out_5[13]), .A12(mult8bit_1_out_5[12]), .A11(mult8bit_1_out_5[11]),
    .A10(mult8bit_1_out_5[10]), .A9(mult8bit_1_out_5[9]), .A8(mult8bit_1_out_5[8]), .A7(mult8bit_1_out_5[7]),
    .A6(mult8bit_1_out_5[6]), .A5(mult8bit_1_out_5[5]), .A4(mult8bit_1_out_5[4]), .A3(mult8bit_1_out_5[3]),
    .A2(mult8bit_1_out_5[2]), .A1(mult8bit_1_out_5[1]), .A0(mult8bit_1_out_5[0]), .U(bintobcd_1_u),
    .T(bintobcd_1_t), .H(bintobcd_1_h), .TH(bintobcd_1_th), .TT(bintobcd_1_tt));
  Button left (.out(left_out));
  scroller scroller_1 (
    .start(d_ff_2_q), .in_2(right_out), .one(scroller_1_one), .two(scroller_1_two), .three(scroller_1_three),
    .left(left_out), .TT(bintobcd_1_tt), .H(bintobcd_1_h), .T(bintobcd_1_t), .U(bintobcd_1_u),
    .TH(bintobcd_1_th));
  Button right (.out(right_out));
  Decoder7Segment decoder7segment_1 (
    .in_1(scroller_1_one), .a(decoder7segment_1_a), .b(decoder7segment_1_b), .c(decoder7segment_1_c),
    .d(decoder7segment_1_d), .e(decoder7segment_1_e), .f(decoder7segment_1_f), .g(decoder7segment_1_g));
  Decoder7Segment decoder7segment_2 (
    .in_1(scroller_1_two), .a(decoder7segment_2_a), .b(decoder7segment_2_b), .c(decoder7segment_2_c),
    .d(decoder7segment_2_d), .e(decoder7segment_2_e), .f(decoder7segment_2_f), .g(decoder7segment_2_g));
  Decoder7Segment decoder7segment_3 (
    .in_1(scroller_1_three), .a(decoder7segment_3_a), .b(decoder7segment_3_b), .c(decoder7segment_3_c),
    .d(decoder7segment_3_d), .e(decoder7segment_3_e), .f(decoder7segment_3_f), .g(decoder7segment_3_g));
  _7_Segment_Display u_7_segment_display_1 (.g(mult8bit_1_out_6));  // open: f, a, b, e, d, c, dp
  _7_Segment_Display u_7_segment_display_2 (
    .g(decoder7segment_1_g), .f(decoder7segment_1_f), .a(decoder7segment_1_a), .b(decoder7segment_1_b),
    .e(decoder7segment_1_e), .d(decoder7segment_1_d), .c(decoder7segment_1_c));  // open: dp
  _7_Segment_Display u_7_segment_display_3 (
    .g(decoder7segment_2_g), .f(decoder7segment_2_f), .a(decoder7segment_2_a), .b(decoder7segment_2_b),
    .e(decoder7segment_2_e), .d(decoder7segment_2_d), .c(decoder7segment_2_c));  // open: dp
  _7_Segment_Display u_7_segment_display_4 (
    .g(decoder7segment_3_g), .f(decoder7segment_3_f), .a(decoder7segment_3_a), .b(decoder7segment_3_b),
    .e(decoder7segment_3_e), .d(decoder7segment_3_d), .c(decoder7segment_3_c));  // open: dp
endmodule

module Decoder7Segment (
  input  [3:0] in_1,
  output a,
  output b,
  output c,
  output d,
  output e,
  output f,
  output g
);

  wire and_1_out, and_2_out, and_3_out, and_4_out, and_5_out, and_6_out, and_7_out, and_8_out, and_9_out,
       and_10_out, and_11_out, and_12_out, and_13_out, and_14_out, and_15_out, and_16_out, and_17_out,
       and_18_out, and_19_out, and_20_out, and_21_out, and_22_out, and_23_out, and_24_out, and_25_out,
       and_26_out, and_27_out, and_28_out, and_29_out, and_30_out, and_31_out, not_1_out, not_2_out,
       not_3_out, not_4_out;

  not not_1 (not_1_out, in_1[3]);
  not not_2 (not_2_out, in_1[2]);
  not not_3 (not_3_out, in_1[1]);
  not not_4 (not_4_out, in_1[0]);
  and and_1 (and_1_out, not_2_out, not_4_out);
  and and_2 (and_2_out, not_1_out, in_1[1]);
  and and_3 (and_3_out, in_1[3], not_3_out);
  and and_4 (and_4_out, in_1[2], in_1[1]);
  and and_5 (and_5_out, not_1_out, not_3_out);
  and and_6 (and_6_out, not_2_out, not_4_out);
  and and_7 (and_7_out, not_1_out, in_1[0]);
  and and_8 (and_8_out, not_3_out, in_1[0]);
  and and_9 (and_9_out, in_1[3], not_2_out);
  and and_10 (and_10_out, not_1_out, not_3_out, not_4_out);
  and and_11 (and_11_out, not_2_out, not_3_out);
  and and_12 (and_12_out, not_1_out, in_1[1], in_1[0]);
  and and_13 (and_13_out, not_1_out, in_1[2], not_4_out);
  and and_14 (and_14_out, not_2_out, in_1[1], in_1[0]);
  and and_15 (and_15_out, not_1_out, not_2_out, not_4_out);
  and and_16 (and_16_out, not_1_out, in_1[1], not_4_out);
  and and_17 (and_17_out, not_2_out, not_3_out, not_4_out);
  and and_18 (and_18_out, in_1[3], not_3_out, not_4_out);
  and and_19 (and_19_out, in_1[2], in_1[1], not_4_out);
  and and_20 (and_20_out, not_2_out, not_4_out);
  and and_21 (and_21_out, not_1_out, in_1[2], not_3_out, in_1[0]);
  and and_22 (and_22_out, in_1[1], not_4_out);
  and and_23 (and_23_out, in_1[3], in_1[1]);
  and and_24 (and_24_out, in_1[3], not_4_out);
  and and_25 (and_25_out, not_3_out, not_4_out);
  and and_26 (and_26_out, in_1[2], not_4_out);
  or or_1 (f, and_25_out, and_26_out, in_1[3]);
  and and_27 (and_27_out, not_2_out, in_1[1]);
  and and_28 (and_28_out, not_1_out, in_1[2], not_4_out);
  and and_29 (and_29_out, in_1[3], not_2_out);
  and and_30 (and_30_out, in_1[3], in_1[0]);
  and and_31 (and_31_out, in_1[1], not_4_out);
  or or_2 (a, and_1_out, and_2_out, and_3_out, and_4_out);
  or or_3 (b, and_5_out, and_6_out, and_7_out, and_8_out);
  or or_4 (c, and_9_out, and_10_out, and_11_out, and_12_out, and_13_out);
  or or_5 (d, and_14_out, and_15_out, and_16_out, and_17_out, and_18_out, and_19_out);
  or or_6 (e, and_20_out, and_21_out, and_22_out, and_23_out, and_24_out);
  or or_7 (g, and_27_out, and_28_out, and_29_out, and_30_out, and_31_out);
endmodule

module segments (
  input  [3:0] in_1
);

  wire decoder7segment_1_a, decoder7segment_1_b, decoder7segment_1_c, decoder7segment_1_d,
       decoder7segment_1_e, decoder7segment_1_f, decoder7segment_1_g;

  Decoder7Segment decoder7segment_1 (
    .in_1(in_1), .a(decoder7segment_1_a), .b(decoder7segment_1_b), .c(decoder7segment_1_c),
    .d(decoder7segment_1_d), .e(decoder7segment_1_e), .f(decoder7segment_1_f), .g(decoder7segment_1_g));
  _7_Segment_Display #(.decimalPoint("false")) u_7_segment_display_1 (
    .g(decoder7segment_1_g), .f(decoder7segment_1_f), .a(decoder7segment_1_a), .b(decoder7segment_1_b),
    .e(decoder7segment_1_e), .d(decoder7segment_1_d), .c(decoder7segment_1_c));
endmodule

module scroller (
  input  start,
  input  in_2,
  input  left,
  input  [3:0] TT,
  input  [3:0] H,
  input  [3:0] T,
  input  [3:0] U,
  input  [3:0] TH,
  output [3:0] one,
  output [3:0] two,
  output [3:0] three
);

  wire not_1_out, or_1_out;
  wire [1:0] counter_1_q;

  not not_1 (not_1_out, in_2);
  or or_1 (or_1_out, in_2, left);
  Multiplexer #(.select(2), .width(4)) multiplexer_1 (
    .in0(H), .in1(TH), .in2(TT), .in3(4'b0000), .out(one), .sel(counter_1_q));
  Multiplexer #(.select(2), .width(4)) multiplexer_2 (
    .in0(T), .in1(H), .in2(TH), .in3(4'b0000), .out(two), .sel(counter_1_q));
  Multiplexer #(.select(2), .width(4)) multiplexer_3 (
    .in0(U), .in1(T), .in2(H), .in3(4'b0000), .out(three), .sel(counter_1_q));
  Counter #(.max('h3), .width(2)) counter_1 (
    .clr(start), .up(not_1_out), .clk(or_1_out), .Q(counter_1_q));  // open: load, count, D, carry
endmodule
